// Logisim project main.circ as structural Verilog
module ram (
  input  [15:0] Address,
  input  [15:0] Data_in,
  input  Clear,
  input  Chip_Select,
  input  Read__0____write__1,
  output [15:0] Data_out
);

  wire and_1_out, not_1_out, not_2_out;
  wire [15:0] ram_1_data;

  not not_1 (not_1_out, Read__0____write__1);
  RAM #(.addrWidth(16), .dataWidth(16), .bus("separate")) ram_1 (
    .addr(Address), .din(Data_in), .data(ram_1_data), .str(Read__0____write__1), .sel(Chip_Select),
    .clk(not_2_out), .ld(not_1_out), .clr(Clear));
  not not_2 (not_2_out, Chip_Select);
  and and_1 (and_1_out, Chip_Select, not_1_out);
  assign Data_out = and_1_out ? ram_1_data : 16'bz;  // Controlled_Buffer controlled_buffer_1

  // Notes on the sheet:
  //   128KB RAM module
endmodule

module cpu (
  input  power_on,
  input  clock,
  input  reset,
  input  [15:0] RAM_data_in,
  output RAM_cs,
  output RAM_r_w,
  output [15:0] RAM_data_out,
  output [15:0] RAM_address,
  output [15:0] OR_output
);

  wire a_ie, b_ie, bkp_ie, bkp_oe, cu_en, flg_ie, hlt, ir_ie, mar_ie, nb, not_1_out, o_ie, o_oe, or_ie,
       r0_ie, r0_oe, r1_ie, r1_oe, r2_ie, r2_oe, r3_ie, r3_oe, r4_ie, r4_oe, r5_ie, r5_oe, r6_ie, r6_oe,
       r7_ie, r7_oe, tmp_ie, tmp_oe;
  wire [2:0] counter_1_q, op_code;
  wire [3:0] alu_1_v_c_z_s, flg_out;
  wire [9:4] multiplexer_1_out;
  wire [15:0] A_output, adder_1_out, alu_1_output, B_output;

  Counter #(.width(3), .max('h5)) counter_1 (
    .count(not_1_out), .Q(counter_1_q), .clk(clock), .clr(reset));  // open: load, D, carry
  not not_1 (not_1_out, hlt);
  Multiplexer #(.select(3), .width(11), .disabled(0)) multiplexer_1 (
    .in0(11'h200), .in1(11'h2), .in2(11'hc8), .in3(11'h410), .in4(11'h104), .in5(11'h41),
    .out({ir_ie, multiplexer_1_out, tmp_ie, tmp_oe, bkp_ie, bkp_oe}), .sel(counter_1_q), .en(power_on));  // open: in6, in7
  reg_16b R0 (
    .Data(RAM_data_in), .Input_Enable(r0_ie), .Clock(clock), .Output(RAM_data_in), .Output_Enable(r0_oe),
    .Clear(reset));
  reg_16b R1 (
    .Data(RAM_data_in), .Input_Enable(r1_ie), .Clock(clock), .Output(RAM_data_in), .Output_Enable(r1_oe),
    .Clear(reset));
  reg_16b R2 (
    .Data(RAM_data_in), .Input_Enable(r2_ie), .Clock(clock), .Output(RAM_data_in), .Output_Enable(r2_oe),
    .Clear(reset));
  reg_16b R3 (
    .Data(RAM_data_in), .Input_Enable(r3_ie), .Clock(clock), .Output(RAM_data_in), .Output_Enable(r3_oe),
    .Clear(reset));
  reg_16b R4 (
    .Data(RAM_data_in), .Input_Enable(r4_ie), .Clock(clock), .Output(RAM_data_in), .Output_Enable(r4_oe),
    .Clear(reset));
  reg_16b SP__R5 (
    .Data(RAM_data_in), .Input_Enable(r5_ie), .Clock(clock), .Output(RAM_data_in), .Output_Enable(r5_oe),
    .Clear(reset));
  reg_16b LR__R6 (
    .Data(RAM_data_in), .Input_Enable(r6_ie), .Clock(clock), .Output(RAM_data_in), .Output_Enable(r6_oe),
    .Clear(reset));
  reg_16b PC__R7 (
    .Data(RAM_data_in), .Input_Enable(r7_ie), .Clock(clock), .Output(RAM_data_in), .Output_Enable(r7_oe),
    .Clear(reset));
  buf and_1 (cu_en, multiplexer_1_out[9]);  // AND_Gate
  buf or_1 (r7_ie, multiplexer_1_out[8]);  // OR_Gate
  buf or_2 (RAM_cs, multiplexer_1_out[4]);  // OR_Gate
  buf or_3 (r7_oe, multiplexer_1_out[7]);  // OR_Gate
  buf or_4 (RAM_r_w, multiplexer_1_out[5]);  // OR_Gate
  buf or_5 (mar_ie, multiplexer_1_out[6]);  // OR_Gate
  reg_16b IR (
    .Data(RAM_data_in), .Input_Enable(ir_ie), .Clock(clock), .Output(RAM_data_in), .Output_Enable(power_on),
    .Clear(reset));
  reg_16b A (
    .Data(RAM_data_in), .Input_Enable(a_ie), .Clock(clock), .Output(A_output), .Output_Enable(power_on),
    .Clear(reset));
  reg_16b OUT (
    .Data(alu_1_output), .Input_Enable(o_ie), .Clock(clock), .Output(RAM_data_in), .Output_Enable(o_oe),
    .Clear(reset));
  reg_16b MAR (
    .Data(RAM_data_in), .Input_Enable(mar_ie), .Clock(clock), .Output(RAM_address), .Output_Enable(power_on),
    .Clear(reset));
  reg_16b OR_6 (
    .Data(RAM_data_in), .Input_Enable(or_ie), .Clock(clock), .Output(OR_output), .Output_Enable(power_on),
    .Clear(reset));
  alu alu_1 (
    .Input_A(A_output), .Input_B(B_output), .nB(nb), .Output(alu_1_output), .Op_code(op_code),
    .V_C_Z_S(alu_1_v_c_z_s));
  reg_16b TMP (
    .Data(adder_1_out), .Input_Enable(tmp_ie), .Clock(clock), .Output(RAM_data_in), .Output_Enable(tmp_oe),
    .Clear(reset));
  Adder #(.width(16)) adder_1 (.a(RAM_data_in), .b({16{1'b0}}), .out(adder_1_out), .cin(power_on));  // open: cout
  reg_16b B (
    .Data(RAM_data_in), .Input_Enable(b_ie), .Clock(clock), .Output(B_output), .Output_Enable(power_on),
    .Clear(reset));
  reg_4b FLAGS (
    .Data(alu_1_v_c_z_s), .Input_Enable(flg_ie), .Clock(clock), .Output(flg_out), .Output_Enable(power_on),
    .Clear(reset));
  reg_16b BKP (
    .Data(RAM_address), .Input_Enable(bkp_ie), .Clock(clock), .Output(RAM_data_in), .Output_Enable(bkp_oe),
    .Clear(reset));

  assign RAM_data_out = RAM_data_in;

  // Other names for the same wires on the sheet: bus[15:0] = RAM_data_in; clear = reset; clk = clock;
  //   OR_out[15:0] = OR_output; pwr = power_on; RAM_addr[15:0] = RAM_address

  // Notes on the sheet:
  //   Fetch-decode-execute cycle
  //   16bit CPU
endmodule

module alu (
  input  [15:0] Input_A,
  input  [15:0] Input_B,
  input  nB,
  input  [2:0] Op_code,
  output [15:0] Output,
  output [3:0] V_C_Z_S
);

  wire xnor_1_out, xor_2_out;
  wire [15:0] adder_1_out, and_1_out, B, not_1_out, not_2_out, or_1_out, shifter_1_out, shifter_2_out,
       shifter_3_out, xor_1_out;

  Multiplexer #(.width(16), .disabled(0), .enable("false")) multiplexer_1 (
    .in0(Input_B), .in1(not_1_out), .out(B), .sel(nB));
  assign not_1_out = ~Input_B;  // NOT_Gate not_1, 16 bits wide
  Adder #(.width(16)) adder_1 (.a(Input_A), .b(B), .out(adder_1_out), .cin(nB), .cout(V_C_Z_S[2]));
  assign and_1_out = Input_A & B;  // AND_Gate and_1, 16 bits wide
  assign or_1_out = Input_A | B;  // OR_Gate or_1, 16 bits wide
  assign xor_1_out = Input_A ^ B;  // XOR_Gate xor_1, 16 bits wide
  assign not_2_out = ~Input_A;  // NOT_Gate not_2, 16 bits wide
  Shifter #(.width(16)) shifter_1 (.in(Input_A), .\dist (B[3:0]), .out(shifter_1_out));
  Shifter #(.width(16), .shift("lr")) shifter_2 (.in(Input_A), .\dist (B[3:0]), .out(shifter_2_out));
  Shifter #(.width(16), .shift("ar")) shifter_3 (.in(Input_A), .\dist (B[3:0]), .out(shifter_3_out));
  Multiplexer #(.select(3), .width(16), .disabled(0), .enable("false")) multiplexer_2 (
    .in0(adder_1_out), .in1(and_1_out), .in2(or_1_out), .in3(xor_1_out), .in4(not_2_out),
    .in5(shifter_1_out), .in6(shifter_2_out), .in7(shifter_3_out), .out(Output), .sel(Op_code));
  xor xor_2 (xor_2_out, Input_A[15], Output[15]);
  xnor xnor_1 (xnor_1_out, Input_A[15], B[15]);
  and and_2 (V_C_Z_S[3], xnor_1_out, xor_2_out);
  Comparator #(.width(16)) comparator_1 (.a(Output), .b({16{1'b0}}), .eq(V_C_Z_S[1]));  // open: gt, lt

  assign V_C_Z_S[0] = Output[15];

  // Other names for the same wires on the sheet: A[15:0] = Input_A; O[15:0] = Output; c_out = V_C_Z_S[2]

  // Notes on the sheet:
  //   16bit ALU
  //   Flags control
endmodule

module reg_16b (
  input  [15:0] Data,
  input  Input_Enable,
  input  Output_Enable,
  input  Clock,
  input  Clear,
  output [15:0] Output
);

  wire and_1_out;
  wire [15:0] register_1_q;

  Register #(.width(16)) register_1 (.D(Data), .en(and_1_out), .Q(register_1_q), .clk(and_1_out), .clr(Clear));
  and and_1 (and_1_out, Input_Enable, ~Clock);  // AND_Gate
  assign Output = Output_Enable ? register_1_q : 16'bz;  // Controlled_Buffer controlled_buffer_1

  // Notes on the sheet:
  //   General purpose 16bit register
endmodule

module reg_4b (
  input  [3:0] Data,
  input  Input_Enable,
  input  Output_Enable,
  input  Clock,
  input  Clear,
  output [3:0] Output
);

  wire and_1_out;
  wire [3:0] register_1_q;

  Register #(.width(4)) register_1 (.D(Data), .en(and_1_out), .Q(register_1_q), .clk(and_1_out), .clr(Clear));
  and and_1 (and_1_out, Input_Enable, ~Clock);  // AND_Gate
  assign Output = Output_Enable ? register_1_q : 4'bz;  // Controlled_Buffer controlled_buffer_1

  // Notes on the sheet:
  //   General purpose 4bit register
endmodule
